# Fritzing sketch Breadboard Diagram (saved by Fritzing 0.9.3b)
breadboards: 2

parts:
  R1 = Resistor [tolerance=±5% resistance=470 package=THT]
  LED2 = RGB LED (com. cathode, rgb) [package="5 mm [THT]"]
  LED3 = RGB LED (com. cathode, rgb) [package="5 mm [THT]"]
  LED4 = RGB LED (com. cathode, rgb) [package="5 mm [THT]"]
  LED5 = RGB LED (com. cathode, rgb) [package="5 mm [THT]"]
  LED6 = RGB LED (com. cathode, rgb) [package="5 mm [THT]"]
  LED7 = RGB LED (com. cathode, rgb) [package="5 mm [THT]"]
  LED8 = RGB LED (com. cathode, rgb) [package="5 mm [THT]"]
  U1 = 74HC595 [package="DIP16 [THT]"]
  U2 = 74HC595 [package="DIP16 [THT]"]
  U3 = 74HC595 [package="DIP16 [THT]"]
  R2 = Resistor [tolerance=±5% resistance=1k package=THT]
  LED1 = RGB LED (com. cathode, rgb) [package="5 mm [THT]"]
  R3 = Resistor [tolerance=±5% resistance=1k package=THT]
  R4 = Resistor [tolerance=±5% resistance=1k package=THT]
  R5 = Resistor [tolerance=±5% resistance=1k package=THT]
  R6 = Resistor [tolerance=±5% resistance=1k package=THT]
  R7 = Resistor [tolerance=±5% resistance=1k package=THT]
  R8 = Resistor [tolerance=±5% resistance=1k package=THT]
  R9 = Resistor [tolerance=±5% resistance=1k package=THT]
  R10 = Resistor [tolerance=±5% resistance=1k package=THT]
  R11 = Resistor [tolerance=±5% resistance=1k package=THT]
  R12 = Resistor [tolerance=±5% resistance=1k package=THT]
  R13 = Resistor [tolerance=±5% resistance=1k package=THT]
  R14 = Resistor [tolerance=±5% resistance=1k package=THT]
  R15 = Resistor [tolerance=±5% resistance=1k package=THT]
  R16 = Resistor [tolerance=±5% resistance=1k package=THT]
  R17 = Resistor [tolerance=±5% resistance=1k package=THT]
  R18 = Resistor [tolerance=±5% resistance=470 package=THT]
  R19 = Resistor [tolerance=±5% resistance=470 package=THT]
  R20 = Resistor [tolerance=±5% resistance=470 package=THT]
  R21 = Resistor [tolerance=±5% resistance=470 package=THT]
  R22 = Resistor [tolerance=±5% resistance=470 package=THT]
  R23 = Resistor [tolerance=±5% resistance=470 package=THT]
  R24 = Resistor [tolerance=±5% resistance=470 package=THT]
  ADC1 = MCP3008 [package=dil16]
  R25 = PHOTOCELL [package=photocell]
  R26 = Resistor [tolerance=±5% resistance=10k package=THT]
  SparkFun1 = SoftPot Membrane Potentiometer - 50mm [part_number=SEN-08680]
  SparkFun2 = SoftPot Membrane Potentiometer - 50mm [part_number=SEN-08680]
  SparkFun3 = SoftPot Membrane Potentiometer - 50mm [part_number=SEN-08680]
  SparkFun4 = SoftPot Membrane Potentiometer - 50mm [part_number=SEN-08680]
  R27 = Resistor [tolerance=±5% resistance=10k package=THT]
  R28 = Resistor [tolerance=±5% resistance=10k package=THT]
  R29 = Resistor [tolerance=±5% resistance=10k package=THT]
  R30 = Resistor [tolerance=±5% resistance=10k package=THT]
  R31 = Resistor [tolerance=±5% resistance=10k package=THT]
  R32 = Resistor [tolerance=±5% resistance=10k package=THT]
  R33 = Resistor [tolerance=±5% resistance=10k package=THT]
  R34 = Resistor [tolerance=±5% resistance=10k package=THT]
  R35 = Resistor [tolerance=±5% resistance=100k package=THT]
  R36 = Resistor [tolerance=±5% resistance=100k package=THT]
  R37 = Resistor [tolerance=±5% resistance=100k package=THT]
  R38 = Resistor [tolerance=±5% resistance=100k package=THT]
  MCU1 = Raspberry Pi Zero

nets:
  N1: R1.Pin_0, U3.Q0
  N2: R1.Pin_1, LED1.red_anode
  N3: LED2.red_anode, R18.Pin_1
  GND: LED2.common_cathode, LED3.common_cathode, LED4.common_cathode, LED6.common_cathode, LED7.common_cathode, LED8.common_cathode, U1.GND, U1.OE, U2.GND, U2.OE, U3.GND, U3.OE, LED1.common_cathode, ADC1.DGND, ADC1.AGND, R26.Pin_0, R27.Pin_0, R29.Pin_0, R31.Pin_0, R33.Pin_0
  N4: LED2.green_anode, R16.Pin_1
  N5: LED2.blue_anode, R17.Pin_1
  N6: LED3.red_anode, R24.Pin_1
  N7: LED3.green_anode, R5.Pin_1
  N8: LED3.blue_anode, R4.Pin_1
  N9: LED4.red_anode, R23.Pin_1
  N10: LED4.green_anode, R7.Pin_1
  N11: LED4.blue_anode, R6.Pin_1
  N12: LED5.red_anode, R22.Pin_1
  N13: LED5.green_anode, R8.Pin_1
  N14: LED5.blue_anode, R9.Pin_1
  N15: LED6.red_anode, R21.Pin_1
  N16: LED6.green_anode, R10.Pin_1
  N17: LED6.blue_anode, R11.Pin_1
  N18: LED7.red_anode, R20.Pin_1
  N19: LED7.green_anode, R12.Pin_1
  N20: LED7.blue_anode, R13.Pin_1
  N21: LED8.red_anode, R19.Pin_1
  N22: LED8.green_anode, R14.Pin_1
  N23: LED8.blue_anode, R15.Pin_1
  N24: U1.Q1, R4.Pin_0
  N25: U1.Q2, R6.Pin_0
  N26: U1.Q3, R9.Pin_0
  N27: U1.Q4, R11.Pin_0
  N28: U1.Q5, R13.Pin_0
  N29: U1.Q6, R15.Pin_0
  N30: U1.Q7, R17.Pin_0
  VCC: U1.MR, U1.VCC, U2.MR, U2.VCC, U3.MR, U3.VCC, ADC1.VREF, ADC1.VDD, R25.P$1, R26.Pin_1, R28.Pin_0, R30.Pin_0, R32.Pin_0, R34.Pin_0, R35.Pin_0, R36.Pin_0, R37.Pin_0, R38.Pin_0, MCU1.pin_1
  N31: U1.SH_CP, U2.SH_CP, U3.SH_CP, MCU1.pin_40
  N32: U1.ST_CP, MCU1.pin_36
  N33: U1.DS, U2.DS, U3.DS, MCU1.pin_38
  N34: U1.Q0, R3.Pin_0
  N35: U2.Q1, R5.Pin_0
  N36: U2.Q2, R7.Pin_0
  N37: U2.Q3, R8.Pin_0
  N38: U2.Q4, R10.Pin_0
  N39: U2.Q5, R12.Pin_0
  N40: U2.Q6, R14.Pin_0
  N41: U2.Q7, R16.Pin_0
  N42: U2.ST_CP, MCU1.pin_5
  N43: U2.Q0, R2.Pin_0
  N44: U3.Q1, R24.Pin_0
  N45: U3.Q2, R23.Pin_0
  N46: U3.Q3, R22.Pin_0
  N47: U3.Q4, R21.Pin_0
  N48: U3.Q5, R20.Pin_0
  N49: U3.Q6, R19.Pin_0
  N50: U3.Q7, R18.Pin_0
  N51: U3.ST_CP, MCU1.pin_12
  N52: R2.Pin_1, LED1.green_anode
  N53: LED1.blue_anode, R3.Pin_1
  N54: ADC1.CH0, R25.P$2
  N55: ADC1.CH1, SparkFun4.wiper, R38.Pin_1
  N56: ADC1.CH2, SparkFun3.wiper, R37.Pin_1
  N57: ADC1.CH3, SparkFun2.wiper, R36.Pin_1
  N58: ADC1.CH4, SparkFun1.wiper, R35.Pin_1
  N59: ADC1.CS/SHDN, MCU1.pin_24
  N60: ADC1.Din, MCU1.pin_19
  N61: ADC1.Dout, MCU1.pin_21
  N62: ADC1.CLK, MCU1.pin_23
  N63: SparkFun1.leg1, R27.Pin_1
  N64: SparkFun1.leg2, R28.Pin_1
  N65: SparkFun2.leg1, R29.Pin_1
  N66: SparkFun2.leg2, R30.Pin_1
  N67: SparkFun3.leg1, R31.Pin_1
  N68: SparkFun3.leg2, R32.Pin_1
  N69: SparkFun4.leg1, R33.Pin_1
  N70: SparkFun4.leg2, R34.Pin_1

custom parts:
  SoftPot Membrane Potentiometer - 50mm: These are very thin variable potentiometers. By pressing down on various parts of the strip, the resistance linearly changes from 100Ohms to 10,000Ohms allowing the user to very accurately calculate the relative position on the strip. Can be used as an accurate positional indicator for CNC head positioning, variable user input (volume level input for example), straight user input (multiple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
